# Fritzing sketch NORTH (saved by Fritzing 0.9.3b)
perfboards: 1

parts:
  Part1 = Adafruit Pro Trinket 3.3V 12MHz [part_number="Adafruit #2010"]
  Part2 = Adafruit Bluefruit LE UART Friend [part_number="Adafruit #2479"]
  Part3 = 9-DOF Absolute Orientation IMU Fusion Breakout - BNO055
  Part4 = Lithium Ion Polymer Battery 3.7v 500mAh [part_number=1578]  # not connected
  Part5 = Adafruit Pro Trinket LiIon/LiPoly Backpack [part_number="Adafruit #2124"]
  S1 = Toggle Switch [package=THT]

nets:
  VIN: Part1.VBAT, Part2.VIN, Part3.3.3V, Part5.VBAT
  GND: Part1.GND, Part2.GND, Part3.GND, Part5.GND
  N1: Part1.VBUS, Part5.VBUS
  N2: Part1.D10, Part2.RTS
  N3: Part1.D11, Part2.RXI
  N4: Part1.D12, Part2.TXO
  N5: Part1.D13, Part2.CTS
  N6: Part1.A4, Part3.SDA_5V
  N7: Part1.A5, Part3.SCL_5V
  N8: Part5.SW2, S1.COM
  N9: Part5.SW1, S1.L2

custom parts:
  Adafruit Pro Trinket 3.3V 12MHz: rinket's got a big sister in town - the Pro Trinket 3V! Pro Trinket combines everything you love about Trinket with the familiarity of the core Arduino chip, the ATmega328. It's like an Arduino Pro Mini with more pins and USB tossed in. Trinket's a year old now, and while its been great to see tons of tiny projects, sometimes you just need more pins, more FLASH, and more RAM. That's why we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
  Adafruit Bluefruit LE UART Friend: The Bluefruit LE UART Friend makes it easy to add Bluetooth Low Energy connectivity to anything with a hardware or software serial port. We even have nice hardware flow control so you won't have to think about losing data. Connect to your Arduino or other microcontroller or even just a standard FTDI cable for debugging and testing.
  9-DOF Absolute Orientation IMU Fusion Breakout - BNO055: A MEMS accelerometer, magnetometer and gyroscope on a single die with a high speed ARM Cortex-M0 based processor to digest all the sensor data, abstract the sensor fusion and real time requirements away, and spit out data you can use in quaternions, Euler angles or vectors.
  Lithium Ion Polymer Battery 3.7v 500mAh: Lithium ion polymer (also known as 'lipo' or 'lipoly') batteries are thin, light and powerful. The output ranges from 4.2V when completely charged to 3.7V. This battery has a capacity of 500mAh for a total of about 1.9 Wh. The batteries come pre-attached with a genuine 2-pin JST-PH connector as shown and include the necessary protection circuitry.
  Adafruit Pro Trinket LiIon/LiPoly Backpack: If you have a Pro Trinket you probably know it's the perfect little size for a portable project. This LiPoly backpack makes it really easy to do! Instead of wiring 2 or 3 boards together to make a charging system, this little PCB sits on top of the Pro Trinket and allows a LiPoly/LiIon battery to plug in. When the Pro Trinket USB port is powered, the battery is recharged automatically. Unplug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
